// Logisim project XOR.circ as structural Verilog: 1 circuit, main circuit main
module main (
  input  A,
  input  B,
  output out_3
);

  wire and_1_out, not_1_out, or_1_out;

  or or_1 (or_1_out, B, A);
  and and_1 (and_1_out, A, B);
  not not_1 (not_1_out, and_1_out);
  and and_2 (out_3, not_1_out, or_1_out);

  // Notes on the sheet:
  //   XOR = (A+B)(A'+B')
endmodule
